# Fritzing sketch comp placement fritzing (saved by Fritzing 0.9.10b)
perfboards: 19

parts:
  S1 = H-Bridge with L298N
  Teensy1 = Teensy 4.0
  S2 = H-Bridge with L298N
  Power_plug1 = Power plug
  M1 = RioRand LM2596
  M2 = RioRand LM2596
  C47 = Ceramic Capacitor [capacitance=100nF voltage=35V package="100 mil [THT, multilayer]"]  # not connected
  C52 = Electrolytic Capacitor [capacitance=1µF voltage=35V package="100 mil [THT, electrolytic]"]  # not connected
  U28 = LM 358 Dual Op-Amp [package="SO 08 [SMD]"]  # not connected
  R47 = TRIMPOT [maximum_resistance=200kΩ knob_status=0.1k% power=0.5W package=trimpot_pth_s3_lock]  # not connected
  JP92 = Header 1 [package=1x01_offset]  # not connected
  JP93 = Header 1 [package=1x01_offset]
  JP94 = Header 1 [package=1x01_offset]  # not connected
  JP95 = Header 1 [package=1x01_offset]  # not connected
  JP96 = Header 1 [package=1x01_offset]  # not connected
  JP97 = Header 1 [package=1x01_offset]  # not connected
  JP98 = Header 1 [package=1x01_offset]  # not connected
  JP99 = Header 1 [package=1x01_offset]  # not connected
  JP100 = Header 1 [package=1x01_offset]  # not connected
  JP101 = Header 1 [package=1x01_offset]  # not connected
  JP102 = Header 1 [package=1x01_offset]  # not connected
  JP103 = Header 1 [package=1x01_offset]  # not connected
  JP104 = Header 1 [package=1x01_offset]  # not connected
  JP105 = Header 1 [package=1x01_offset]  # not connected
  JP106 = Header 1 [package=1x01_offset]  # not connected
  JP107 = Header 1 [package=1x01_offset]  # not connected
  JP108 = Header 1 [package=1x01_offset]  # not connected
  JP109 = Header 1 [package=1x01_offset]  # not connected
  JP110 = Header 1 [package=1x01_offset]  # not connected
  JP111 = Header 1 [package=1x01_offset]  # not connected
  U29 = LM 358 Dual Op-Amp [package="SO 08 [SMD]"]  # not connected
  R48 = TRIMPOT [maximum_resistance=200kΩ knob_status=0.1k% power=0.5W package=trimpot_pth_s3_lock]  # not connected
  U30 = LM 358 Dual Op-Amp [package="SO 08 [SMD]"]  # not connected
  R49 = TRIMPOT [maximum_resistance=200kΩ knob_status=0.1k% power=0.5W package=trimpot_pth_s3_lock]  # not connected
  U31 = LM 358 Dual Op-Amp [package="SO 08 [SMD]"]  # not connected
  R50 = TRIMPOT [maximum_resistance=200kΩ knob_status=0.1k% power=0.5W package=trimpot_pth_s3_lock]  # not connected
  U32 = LM 358 Dual Op-Amp [package="SO 08 [SMD]"]  # not connected
  R51 = TRIMPOT [maximum_resistance=200kΩ knob_status=0.1k% power=0.5W package=trimpot_pth_s3_lock]  # not connected
  C53 = Electrolytic Capacitor [capacitance=1µF voltage=35V package="100 mil [THT, electrolytic]"]  # not connected
  C54 = Ceramic Capacitor [capacitance=100nF voltage=35V package="100 mil [THT, multilayer]"]  # not connected
  C55 = Electrolytic Capacitor [capacitance=1µF voltage=35V package="100 mil [THT, electrolytic]"]  # not connected
  C56 = Ceramic Capacitor [capacitance=100nF voltage=35V package="100 mil [THT, multilayer]"]  # not connected
  C57 = Electrolytic Capacitor [capacitance=1µF voltage=35V package="100 mil [THT, electrolytic]"]  # not connected
  C58 = Ceramic Capacitor [capacitance=100nF voltage=35V package="100 mil [THT, multilayer]"]  # not connected
  C59 = Electrolytic Capacitor [capacitance=1µF voltage=35V package="100 mil [THT, electrolytic]"]  # not connected
  C60 = Ceramic Capacitor [capacitance=100nF voltage=35V package="100 mil [THT, multilayer]"]  # not connected
  R52 = Resistor [tolerance=±5% resistance=100 package="0805 [SMD]"]  # not connected
  R53 = Resistor [tolerance=±5% resistance=100 package="0805 [SMD]"]  # not connected
  R54 = Resistor [tolerance=±5% resistance=100 package="0805 [SMD]"]
  R55 = Resistor [tolerance=±5% resistance=100 package="0805 [SMD]"]  # not connected
  JP112 = Header 1 [package=1x01_offset]  # not connected
  JP113 = Header 1 [package=1x01_offset]  # not connected
  JP114 = Header 1 [package=1x01_offset]  # not connected
  JP115 = Header 1 [package=1x01_offset]  # not connected
  JP116 = Header 1 [package=1x01_offset]  # not connected
  JP117 = Header 1 [package=1x01_offset]  # not connected
  JP118 = Header 1 [package=1x01_offset]
  JP119 = Header 1 [package=1x01_offset]  # not connected
  JP120 = Header 1 [package=1x01_offset]  # not connected
  JP121 = Header 1 [package=1x01_offset]  # not connected
  R56 = Resistor [tolerance=±5% resistance=100 package="0805 [SMD]"]
  D6 = Zener Diode [part_number=1N4732A breakdown_voltage=3.3V package="Melf DO-213 AB [SMD]"]  # not connected
  D7 = Zener Diode [part_number=1N4732A breakdown_voltage=3.3V package="Melf DO-213 AB [SMD]"]  # not connected
  D8 = Zener Diode [part_number=1N4732A breakdown_voltage=3.3V package="Melf DO-213 AB [SMD]"]
  D9 = Zener Diode [part_number=1N4732A breakdown_voltage=3.3V package="Melf DO-213 AB [SMD]"]  # not connected
  D10 = Zener Diode [part_number=1N4732A breakdown_voltage=3.3V package="Melf DO-213 AB [SMD]"]  # not connected
  JP122 = Header 1 [package=1x01_offset]  # not connected
  JP123 = Header 1 [package=1x01_offset]
  JP124 = Header 1 [package=1x01_offset]
  JP125 = Header 1 [package=1x01_offset]  # not connected
  JP126 = Header 1 [package=1x01_offset]  # not connected
  JP127 = Header 1 [package=1x01_offset]  # not connected
  JP128 = Header 1 [package=1x01_offset]
  JP129 = Header 1 [package=1x01_offset]
  JP130 = Header 1 [package=1x01_offset]  # not connected
  JP131 = Header 1 [package=1x01_offset]  # not connected
  JP132 = Header 1 [package=1x01_offset]  # not connected
  JP133 = Header 1 [package=1x01_offset]
  JP134 = Header 1 [package=1x01_offset]  # not connected
  JP135 = Header 1 [package=1x01_offset]  # not connected
  JP136 = Header 1 [package=1x01_offset]  # not connected
  U34 = LM 358 Dual Op-Amp [package="SO 08 [SMD]"]  # not connected
  R59 = TRIMPOT [maximum_resistance=10kΩ knob_status=50% power=0.5W package=trimpot_pth_s3_lock]  # not connected
  R60 = TRIMPOT [maximum_resistance=10kΩ knob_status=50% power=0.5W package=trimpot_pth_s3_lock]  # not connected
  JP137 = Header 1 [package=1x01_offset]  # not connected
  JP138 = Header 1 [package=1x01_offset]  # not connected
  JP139 = Header 1 [package=1x01_offset]  # not connected
  JP140 = Header 1 [package=1x01_offset]  # not connected
  JP141 = Header 1 [package=1x01_offset]
  JP142 = Header 1 [package=1x01_offset]
  R61 = TRIMPOT [maximum_resistance=10kΩ knob_status=50% power=0.5W package=trimpot_pth_s3_lock]
  R62 = TRIMPOT [maximum_resistance=10kΩ knob_status=50% power=0.5W package=trimpot_pth_s3_lock]
  U35 = LM 358 Dual Op-Amp [package="SO 08 [SMD]"]  # not connected
  JP143 = Header 1 [package=1x01_offset]
  JP144 = Header 1 [package=1x01_offset]
  JP145 = Header 1 [package=1x01_offset]
  JP146 = Header 1 [package=1x01_offset]
  JP147 = Header 1 [package=1x01_offset]  # not connected
  JP148 = Header 1 [package=1x01_offset]
  JP149 = Header 1 [package=1x01_offset]
  JP150 = Header 1 [package=1x01_offset]  # not connected
  JP151 = Header 1 [package=1x01_offset]  # not connected
  JP152 = Header 1 [package=1x01_offset]  # not connected
  JP153 = Header 1 [package=1x01_offset]
  R63 = Resistor [tolerance=±5% resistance=100 package="0805 [SMD]"]
  R64 = Resistor [tolerance=±5% resistance=100 package="0805 [SMD]"]
  R65 = Resistor [tolerance=±5% resistance=100 package="0805 [SMD]"]
  R66 = Resistor [tolerance=±5% resistance=100 package="0805 [SMD]"]
  R67 = Resistor [tolerance=±5% resistance=100 package="0805 [SMD]"]
  D11 = Zener Diode [part_number=1N4732A breakdown_voltage=3.3V package="Melf DO-213 AB [SMD]"]
  D12 = Zener Diode [part_number=1N4732A breakdown_voltage=3.3V package="Melf DO-213 AB [SMD]"]
  D13 = Zener Diode [part_number=1N4732A breakdown_voltage=3.3V package="Melf DO-213 AB [SMD]"]
  D14 = Zener Diode [part_number=1N4732A breakdown_voltage=3.3V package="Melf DO-213 AB [SMD]"]
  D15 = Zener Diode [part_number=1N4732A breakdown_voltage=3.3V package="Melf DO-213 AB [SMD]"]
  JP166 = Header 1 [package=1x01_offset]  # not connected
  JP168 = Header 1 [package=1x01_offset]  # not connected
  JP174 = Header 1 [package=1x01_offset]  # not connected
  JP175 = Header 1 [package=1x01_offset]  # not connected
  JP176 = Header 1 [package=1x01_offset]  # not connected
  JP177 = Header 1 [package=1x01_offset]  # not connected
  JP178 = Header 1 [package=1x01_offset]  # not connected
  JP179 = Header 1 [package=1x01_offset]  # not connected
  JP180 = Header 1 [package=1x01_offset]  # not connected
  R10 = TRIMPOT [maximum_resistance=10kΩ knob_status=50% power=0.5W package=trimpot_pth_s3_lock]  # not connected
  R6 = TRIMPOT [maximum_resistance=10kΩ knob_status=50% power=0.5W package=trimpot_pth_s3_lock]  # not connected
  R5 = TRIMPOT [maximum_resistance=10kΩ knob_status=50% power=0.5W package=trimpot_pth_s3_lock]  # not connected
  R4 = TRIMPOT [maximum_resistance=10kΩ knob_status=50% power=0.5W package=trimpot_pth_s3_lock]  # not connected
  R9 = TRIMPOT [maximum_resistance=10kΩ knob_status=50% power=0.5W package=trimpot_pth_s3_lock]  # not connected
  JP181 = Header 1 [package=1x01_offset]  # not connected
  JP182 = Header 1 [package=1x01_offset]  # not connected
  JP183 = Header 1 [package=1x01_offset]  # not connected
  JP184 = Header 1 [package=1x01_offset]  # not connected
  JP185 = Header 1 [package=1x01_offset]  # not connected
  JP186 = Header 1 [package=1x01_offset]  # not connected
  JP187 = Header 1 [package=1x01_offset]  # not connected
  R73 = TRIMPOT [maximum_resistance=10kΩ knob_status=50% power=0.5W package=trimpot_pth_s3_lock]
  R74 = TRIMPOT [maximum_resistance=10kΩ knob_status=50% power=0.5W package=trimpot_pth_s3_lock]
  R75 = TRIMPOT [maximum_resistance=10kΩ knob_status=50% power=0.5W package=trimpot_pth_s3_lock]
  R76 = TRIMPOT [maximum_resistance=10kΩ knob_status=50% power=0.5W package=trimpot_pth_s3_lock]
  R77 = TRIMPOT [maximum_resistance=10kΩ knob_status=50% power=0.5W package=trimpot_pth_s3_lock]
  JP188 = Header 1 [package=1x01_offset]
  JP189 = Header 1 [package=1x01_offset]
  JP190 = Header 1 [package=1x01_offset]
  JP191 = Header 1 [package=1x01_offset]
  JP192 = Header 1 [package=1x01_offset]
  JP193 = Header 1 [package=1x01_offset]
  JP194 = Header 1 [package=1x01_offset]
  U51 = mystery part, 3 pins [chip_label=y1]
  U52 = mystery part, 3 pins [chip_label=y2]
  U53 = mystery part, 3 pins [chip_label=x2]
  U54 = mystery part, 3 pins [chip_label=z]  # not connected
  H3 = polarizedheader 4pin 0.156in [package=THT]  # not connected
  H4 = polarizedheader 4pin 0.156in [package=THT]
  C71 = Electrolytic Capacitor [capacitance=1µF voltage=35V package="100 mil [THT, electrolytic]"]
  C72 = Ceramic Capacitor [capacitance=100nF voltage=35V package="100 mil [THT, multilayer]"]
  C73 = Electrolytic Capacitor [capacitance=1µF voltage=35V package="100 mil [THT, electrolytic]"]
  C74 = Ceramic Capacitor [capacitance=100nF voltage=35V package="100 mil [THT, multilayer]"]
  C75 = Electrolytic Capacitor [capacitance=1µF voltage=35V package="100 mil [THT, electrolytic]"]
  C76 = Ceramic Capacitor [capacitance=100nF voltage=35V package="100 mil [THT, multilayer]"]
  C77 = Electrolytic Capacitor [capacitance=1µF voltage=35V package="100 mil [THT, electrolytic]"]
  C78 = Ceramic Capacitor [capacitance=100nF voltage=35V package="100 mil [THT, multilayer]"]
  JP216 = Header 1 [package=1x01_offset]
  JP217 = Header 1 [package=1x01_offset]
  JP218 = Header 1 [package=1x01_offset]
  JP219 = Header 1 [package=1x01_offset]
  JP220 = Header 1 [package=1x01_offset]
  JP221 = Header 1 [package=1x01_offset]
  JP222 = Header 1 [package=1x01_offset]
  JP223 = Header 1 [package=1x01_offset]
  JP224 = Header 1 [package=1x01_offset]
  JP225 = Header 1 [package=1x01_offset]
  JP226 = Header 1 [package=1x01_offset]
  JP227 = Header 1 [package=1x01_offset]
  JP228 = Header 1 [package=1x01_offset]
  JP229 = Header 1 [package=1x01_offset]
  JP230 = Header 1 [package=1x01_offset]
  JP231 = Header 1 [package=1x01_offset]
  JP232 = Header 1 [package=1x01_offset]
  JP233 = Header 1 [package=1x01_offset]
  JP235 = Header 1 [package=1x01_offset]
  R78 = TRIMPOT [maximum_resistance=200kΩ knob_status=0.1k% power=0.5W package=trimpot_pth_s3_lock]  # not connected
  R79 = TRIMPOT [maximum_resistance=200kΩ knob_status=0.1k% power=0.5W package=trimpot_pth_s3_lock]  # not connected
  R80 = TRIMPOT [maximum_resistance=200kΩ knob_status=0.1k% power=0.5W package=trimpot_pth_s3_lock]  # not connected
  R81 = TRIMPOT [maximum_resistance=200kΩ knob_status=0.1k% power=0.5W package=trimpot_pth_s3_lock]  # not connected
  R82 = TRIMPOT [maximum_resistance=200kΩ knob_status=0.1k% power=0.5W package=trimpot_pth_s3_lock]  # not connected
  C79 = Electrolytic Capacitor [capacitance=1µF voltage=35V package="100 mil [THT, electrolytic]"]
  U56 = LM 358 Dual Op-Amp [package="SO 08 [SMD]"]
  U57 = LM 358 Dual Op-Amp [package="SO 08 [SMD]"]
  U58 = LM 358 Dual Op-Amp [package="SO 08 [SMD]"]
  U59 = LM 358 Dual Op-Amp [package="SO 08 [SMD]"]
  U60 = LM 358 Dual Op-Amp [part_number=AD623 package="SO 08 [SMD]"]
  C80 = Ceramic Capacitor [capacitance=100nF voltage=35V package="100 mil [THT, multilayer]"]
  R83 = Resistor [tolerance=±5% resistance=100 package="0805 [SMD]"]
  R84 = Resistor [tolerance=±5% resistance=100 package="0805 [SMD]"]
  R85 = Resistor [tolerance=±5% resistance=100 package="0805 [SMD]"]
  R86 = Resistor [tolerance=±5% resistance=100 package="0805 [SMD]"]
  JP236 = Header 1 [package=1x01_offset]
  JP237 = Header 1 [package=1x01_offset]
  JP238 = Header 1 [package=1x01_offset]
  JP239 = Header 1 [package=1x01_offset]
  JP240 = Header 1 [package=1x01_offset]
  JP241 = Header 1 [package=1x01_offset]
  JP242 = Header 1 [package=1x01_offset]
  JP243 = Header 1 [package=1x01_offset]
  JP244 = Header 1 [package=1x01_offset]
  R87 = Resistor [tolerance=±5% resistance=100 package="0805 [SMD]"]
  D16 = Zener Diode [part_number=1N4732A breakdown_voltage=3.3V package="Melf DO-213 AB [SMD]"]
  D17 = Zener Diode [part_number=1N4732A breakdown_voltage=3.3V package="Melf DO-213 AB [SMD]"]
  D18 = Zener Diode [part_number=1N4732A breakdown_voltage=3.3V package="Melf DO-213 AB [SMD]"]
  D19 = Zener Diode [part_number=1N4732A breakdown_voltage=3.3V package="Melf DO-213 AB [SMD]"]
  D20 = Zener Diode [part_number=1N4732A breakdown_voltage=3.3V package="Melf DO-213 AB [SMD]"]
  JP246 = Header 1 [package=1x01_offset]
  JP247 = Header 1 [package=1x01_offset]
  JP248 = Header 1 [package=1x01_offset]
  JP249 = Header 1 [package=1x01_offset]
  U61 = LM 358 Dual Op-Amp [package="SO 08 [SMD]"]  # not connected
  R88 = TRIMPOT [maximum_resistance=10kΩ knob_status=50% power=0.5W package=trimpot_pth_s3_lock]
  R89 = TRIMPOT [maximum_resistance=10kΩ knob_status=50% power=0.5W package=trimpot_pth_s3_lock]
  JP245 = Header 1 [package=1x01_offset]
  JP250 = Header 1 [package=1x01_offset]
  JP251 = Header 1 [package=1x01_offset]
  JP252 = Header 1 [package=1x01_offset]
  JP254 = Header 1 [package=1x01_offset]
  JP255 = Header 1 [package=1x01_offset]
  JP256 = Header 1 [package=1x01_offset]
  R90 = TRIMPOT [maximum_resistance=10kΩ knob_status=50% power=0.5W package=trimpot_pth_s3_lock]
  R91 = TRIMPOT [maximum_resistance=10kΩ knob_status=50% power=0.5W package=trimpot_pth_s3_lock]
  R92 = TRIMPOT [maximum_resistance=10kΩ knob_status=50% power=0.5W package=trimpot_pth_s3_lock]
  R93 = TRIMPOT [maximum_resistance=10kΩ knob_status=50% power=0.5W package=trimpot_pth_s3_lock]
  R94 = TRIMPOT [maximum_resistance=10kΩ knob_status=50% power=0.5W package=trimpot_pth_s3_lock]
  JP234 = Header 1 [package=1x01_offset]
  JP253 = Header 1 [package=1x01_offset]
  JP258 = Header 1 [package=1x01_offset]
  H11 = polarizedheader 4pin 0.156in [package=THT]
  H12 = polarizedheader 4pin 0.156in [package=THT]
  H13 = polarizedheader 4pin 0.156in [package=THT]
  H14 = polarizedheader 4pin 0.156in [package=THT]
  JP266 = Header 1 [package=1x01_offset]
  JP267 = Header 1 [package=1x01_offset]
  JP268 = Header 1 [package=1x01_offset]  # not connected
  JP269 = Header 1 [package=1x01_offset]  # not connected
  JP270 = Header 1 [package=1x01_offset]  # not connected
  JP271 = Header 1 [package=1x01_offset]  # not connected
  JP272 = Header 1 [package=1x01_offset]  # not connected
  JP273 = Header 1 [package=1x01_offset]  # not connected
  JP274 = Header 1 [package=1x01_offset]
  C81 = Electrolytic Capacitor [capacitance=1µF voltage=35V package="100 mil [THT, electrolytic]"]
  C82 = Ceramic Capacitor [capacitance=100nF voltage=35V package="100 mil [THT, multilayer]"]
  C83 = Electrolytic Capacitor [capacitance=1µF voltage=35V package="100 mil [THT, electrolytic]"]
  C84 = Ceramic Capacitor [capacitance=100nF voltage=35V package="100 mil [THT, multilayer]"]
  C85 = Electrolytic Capacitor [capacitance=1µF voltage=35V package="100 mil [THT, electrolytic]"]
  C86 = Ceramic Capacitor [capacitance=100nF voltage=35V package="100 mil [THT, multilayer]"]
  C87 = Electrolytic Capacitor [capacitance=1µF voltage=35V package="100 mil [THT, electrolytic]"]
  C88 = Ceramic Capacitor [capacitance=100nF voltage=35V package="100 mil [THT, multilayer]"]
  JP275 = Header 1 [package=1x01_offset]  # not connected
  JP276 = Header 1 [package=1x01_offset]
  JP277 = Header 1 [package=1x01_offset]
  JP278 = Header 1 [package=1x01_offset]  # not connected
  JP279 = Header 1 [package=1x01_offset]
  JP280 = Header 1 [package=1x01_offset]
  JP281 = Header 1 [package=1x01_offset]
  JP282 = Header 1 [package=1x01_offset]  # not connected
  JP283 = Header 1 [package=1x01_offset]  # not connected
  JP284 = Header 1 [package=1x01_offset]  # not connected
  JP285 = Header 1 [package=1x01_offset]
  JP286 = Header 1 [package=1x01_offset]  # not connected
  JP287 = Header 1 [package=1x01_offset]  # not connected
  JP288 = Header 1 [package=1x01_offset]  # not connected
  JP289 = Header 1 [package=1x01_offset]  # not connected
  JP290 = Header 1 [package=1x01_offset]  # not connected
  JP291 = Header 1 [package=1x01_offset]  # not connected
  JP292 = Header 1 [package=1x01_offset]  # not connected
  JP293 = Header 1 [package=1x01_offset]  # not connected
  JP294 = Header 1 [package=1x01_offset]  # not connected
  JP295 = Header 1 [package=1x01_offset]  # not connected
  R95 = TRIMPOT [maximum_resistance=200kΩ knob_status=0.1k% power=0.5W package=trimpot_pth_s3_lock]  # not connected
  R96 = TRIMPOT [maximum_resistance=200kΩ knob_status=0.1k% power=0.5W package=trimpot_pth_s3_lock]  # not connected
  R97 = TRIMPOT [maximum_resistance=200kΩ knob_status=0.1k% power=0.5W package=trimpot_pth_s3_lock]  # not connected
  R98 = TRIMPOT [maximum_resistance=200kΩ knob_status=0.1k% power=0.5W package=trimpot_pth_s3_lock]  # not connected
  C89 = Electrolytic Capacitor [capacitance=1µF voltage=35V package="100 mil [THT, electrolytic]"]
  U67 = LM 358 Dual Op-Amp [package="SO 08 [SMD]"]
  U68 = LM 358 Dual Op-Amp [package="SO 08 [SMD]"]
  U69 = LM 358 Dual Op-Amp [package="SO 08 [SMD]"]
  U70 = LM 358 Dual Op-Amp [package="SO 08 [SMD]"]
  U71 = LM 358 Dual Op-Amp [part_number=AD623 package="SO 08 [SMD]"]
  C90 = Ceramic Capacitor [capacitance=100nF voltage=35V package="100 mil [THT, multilayer]"]
  JP296 = Header 1 [package=1x01_offset]  # not connected
  R99 = TRIMPOT [maximum_resistance=200kΩ knob_status=0.1k% power=0.5W package=trimpot_pth_s3_lock]  # not connected
  JP297 = Header 1 [package=1x01_offset]
  JP298 = Header 1 [package=1x01_offset]  # not connected
  C98 = Ceramic Capacitor [capacitance=100nF voltage=35V package="100 mil [THT, multilayer]"]
  JP299 = Header 1 [package=1x01_offset]  # not connected
  JP300 = Header 1 [package=1x01_offset]
  JP301 = Header 1 [package=1x01_offset]
  JP302 = Header 1 [package=1x01_offset]  # not connected
  JP303 = Header 1 [package=1x01_offset]  # not connected
  JP304 = Header 1 [package=1x01_offset]
  JP305 = Header 1 [package=1x01_offset]
  JP306 = Header 1 [package=1x01_offset]  # not connected
  JP307 = Header 1 [package=1x01_offset]  # not connected
  JP308 = Header 1 [package=1x01_offset]  # not connected
  JP309 = Header 1 [package=1x01_offset]  # not connected
  JP310 = Header 1 [package=1x01_offset]  # not connected
  JP311 = Header 1 [package=1x01_offset]  # not connected
  JP312 = Header 1 [package=1x01_offset]  # not connected
  JP313 = Header 1 [package=1x01_offset]  # not connected
  JP314 = Header 1 [package=1x01_offset]  # not connected
  JP315 = Header 1 [package=1x01_offset]  # not connected
  JP316 = Header 1 [package=1x01_offset]  # not connected
  JP317 = Header 1 [package=1x01_offset]  # not connected
  JP318 = Header 1 [package=1x01_offset]  # not connected
  JP319 = Header 1 [package=1x01_offset]  # not connected
  JP320 = Header 1 [package=1x01_offset]  # not connected
  JP321 = Header 1 [package=1x01_offset]
  JP322 = Header 1 [package=1x01_offset]
  U50 = mystery part, 3 pins [chip_label=x1]
  JP323 = Header 1 [package=1x01_offset]  # not connected
  JP324 = Header 1 [package=1x01_offset]  # not connected
  U72 = mystery part, 3 pins [chip_label=z]  # not connected
  U73 = mystery part, 3 pins [chip_label=y2]  # not connected
  U74 = mystery part, 3 pins [chip_label=x2]  # not connected
  H15 = polarizedheader 4pin 0.156in [package=THT]  # not connected
  H16 = polarizedheader 4pin 0.156in [package=THT]  # not connected
  U75 = mystery part, 3 pins [chip_label=x1]  # not connected
  U76 = mystery part, 3 pins [chip_label=y1]  # not connected
  JP325 = Header 1 [package=1x01_offset]
  JP326 = Header 1 [package=1x01_offset]
  H17 = polarizedheader 4pin 0.156in [package=THT]  # not connected
  H18 = polarizedheader 4pin 0.156in [package=THT]

nets:
  12V: S1.12V, S2.12V, Power_plug1.VCC, M1.Pin_2, M2.Pin_2
  GND: S1.GND, S2.GND, Power_plug1.GND, M1.Pin_1, M2.Pin_1
  N1: S1.ENA, Teensy1.pin_4
  N2: S1.IN1, Teensy1.pin_5
  N3: S1.IN2, Teensy1.pin_6
  N4: S1.IN3, Teensy1.pin_7
  N5: S1.IN4, Teensy1.pin_8
  N6: S1.ENB, Teensy1.pin_9
  N7: S1.M1-01, H12.pin1
  N8: S1.M1-02, H12.pin2
  N9: S1.M2-01, H12.pin3
  N10: S1.M2-02, H12.pin4
  N11: Teensy1.pin_1, Teensy1.pin_32, M1.Pin_4
  N12: Teensy1.pin_10, S2.ENA
  N13: Teensy1.pin_11, S2.IN1
  N14: Teensy1.pin_12, S2.IN2
  N15: Teensy1.pin_13, S2.IN3
  N16: Teensy1.pin_14, S2.IN4
  N17: Teensy1.pin_21, S2.ENB
  N18: Teensy1.pin_22, JP240.1
  N19: Teensy1.pin_23, JP239.1, R87.Pin_0, D16.cathode
  N20: Teensy1.pin_24, JP237.1, D16.anode, D17.anode, D18.anode, D19.anode, D20.anode, JP246.1, JP258.1
  N21: Teensy1.pin_25, JP224.1, U58.connector5, R85.Pin_1, JP236.1, JP242.1
  N22: Teensy1.pin_26, R85.Pin_0, JP238.1, D20.cathode
  N23: Teensy1.pin_27, JP220.1, JP247.1, JP274.1
  N24: Teensy1.pin33, M1.Pin_3
  N25: S2.M1-01, H11.pin1
  N26: S2.M1-02, H11.pin2
  N27: S2.M2-01, H11.pin3
  N28: S2.M2-02, H11.pin4
  N29: JP93.1, JP297.1
  N30: R54.Pin_1, JP118.1
  N31: R56.Pin_0, D8.anode
  N32: JP123.1, JP129.1
  N33: JP124.1, JP128.1, JP133.1
  N34: JP141.1, R61.WIPER
  N35: JP142.1, R62.CCW
  N36: R61.CCW, R62.WIPER
  N37: JP143.1, JP149.1, R65.Pin_1
  N38: JP144.1, JP148.1, JP153.1, D11.anode, D12.anode, D13.anode, D14.anode, D15.anode
  N39: JP145.1, R65.Pin_0, D15.cathode
  N40: JP146.1, R67.Pin_0, D11.cathode
  N41: R63.Pin_0, D12.cathode
  N42: R64.Pin_0, D14.cathode
  N43: R66.Pin_0, D13.cathode
  N44: R73.WIPER, JP189.1
  N45: R74.WIPER, JP190.1
  N46: R75.WIPER, JP191.1
  N47: R76.WIPER, JP192.1
  N48: R77.CCW, JP194.1
  N49: R77.WIPER, JP188.1
  N50: R77.CW, JP193.1
  N51: U51.pin1, U52.pin1, U53.pin1, H4.pin1, JP321.1, U50.pin1
  N52: U51.pin2, U52.pin2, U53.pin2, H4.pin2, H4.pin3, H4.pin4, JP322.1, U50.pin2
  N53: C71.+, U59.connector6
  N54: C72.0, C74.0, C76.0, C78.0, JP216.1, JP217.1, C80.0, JP248.1, R88.WIPER
  N55: C73.+, U58.connector6
  N56: C75.+, U57.connector6
  N57: C77.+, U56.connector6
  N58: JP218.1, JP249.1, R89.CCW
  N59: JP219.1, C79.+, U60.connector6
  N60: JP221.1, JP243.1
  N61: JP222.1, R83.Pin_1, JP241.1
  N62: JP223.1, R87.Pin_1, JP245.1
  N63: JP225.1, JP244.1
  N64: JP226.1, JP250.1, R94.WIPER
  N65: JP227.1, H14.pin3
  N66: JP228.1, JP251.1, R90.WIPER
  N67: JP229.1, H14.pin1
  N68: JP230.1, H14.pin2
  N69: JP231.1, JP254.1, R93.WIPER
  N70: JP232.1, H13.pin1
  N71: JP233.1, JP252.1, R91.WIPER
  N72: JP235.1, H14.pin4
  N73: U58.connector4, U60.connector4
  N74: R84.Pin_0, D19.cathode
  N75: R86.Pin_0, D18.cathode
  N76: R88.CCW, R89.WIPER
  N77: JP255.1, R94.CW, JP266.1
  N78: JP256.1, R94.CCW, JP267.1
  N79: R92.WIPER, JP234.1, JP253.1
  N80: C81.+, U70.connector6
  N81: C82.0, C84.0, C86.0, C88.0, JP276.1, JP277.1, C90.0
  N82: C83.+, U69.connector6
  N83: C85.+, U68.connector6
  N84: C87.+, U67.connector6
  N85: JP279.1, C89.+, U71.connector6
  N86: JP280.1, JP281.1
  N87: JP285.1, U69.connector5
  N88: U69.connector4, U71.connector4
  N89: C98.0, JP300.1, JP301.1
  N90: JP304.1, JP305.1
  N91: JP325.1, H18.pin1
  N92: JP326.1, H18.pin2

notes:
  3V3
  +5V
  X1
  Y1
  Y2
  X2
  12V
  AB  AB
  A
  B
  X1  Y1
  X2  Y2
  x1
  y1
  x2
  z
  GND
  y2

custom parts:
  H-Bridge with L298N: h-bridge
  Teensy 4.0: The Teensy is a complete USB-based microcontoller development system, in a very small footprint, capable of implementing many types of projects. All programming is done via the USB port. No special programmer is needed, only a standard micro-USB cable and a PC or Macintosh with a USB port.
